# Fritzing sketch 28BYJ-48 motor with ULN2003 driver board (saved by Fritzing 0.9.9b)

parts:
  Part1 = Arduino Uno (Rev3)
  Driver1 = 28BYJ-48 Driver Module [part_number=ULN2003 package=THT]
  SM1 = 28BYJ-48 Stepper Motor [part_number=28BYJ-48]
  Power_plug1 = Power plug

nets:
  N1: Part1.D8, Driver1.IN4
  N2: Part1.D9_PWM, Driver1.IN3
  N3: Part1.D10_PWM/SS, Driver1.IN2
  N4: Part1.D11_PWM/MOSI, Driver1.IN1
  GND: Driver1.GND, Power_plug1.GND
  N5: Driver1.Vmotor, Power_plug1.VCC
  N6: Driver1.blue-pin, SM1.blue-pin
  N7: Driver1.pink-pin, SM1.pink-pin
  N8: Driver1.yellow-pin, SM1.yellow-pin
  N9: Driver1.orange-pin, SM1.orange-pin
  N10: Driver1.red-pin, SM1.red-pin

custom parts:
  28BYJ-48 Driver Module: ULN2003 Driver Module for the 28BYJ-48 Unipolar Stepper Motor LED A - Blue wire - Bottom coil left LED B - Pink wire - Top coil left LED C - Yellow wire - Bottom coil right LED D - Orange wire - Top coil right Common rail - red Connector pins: blue - pink - yellow - orange - red Control pins - IN1 to IN4 Power pins - GND & Vmotor (5-12V) On/Off jumper (if removed, power to motor is cut).
  28BYJ-48 Stepper Motor: Unipolar Stepper Motor 28BYJ-48 Top coil - pink & orange Bottom coil - blue & yellow Common rail - red Connector pins: blue - pink - yellow - orange - red
